# Fritzing sketch Untitled Sketch (saved by Fritzing 0.9.3b)
circuit board: 26.4583cm x 10.8797cm
breadboards: 1

parts:
  Composant1 = Arduino Leonardo (Rev3b)  # not connected
  Composant2 = Arduino Motor Shield (Rev3)
  hc-sr1 = hc-sr04
  M1 = DC Motor
  hc-sr2 = hc-sr04
  hc-sr3 = hc-sr04
  M2 = DC Motor

nets:
  VCC: Composant2.5V, hc-sr1.VCC, hc-sr2.VCC, hc-sr3.VCC
  N1: Composant2.A2, hc-sr1.Trig
  N2: Composant2.A3, hc-sr1.Echo
  N3: Composant2.D8/BreakeB, hc-sr3.Echo
  GND: Composant2.GND, hc-sr1.GND, hc-sr2.GND, hc-sr3.GND
  N4: Composant2.D2, hc-sr3.Trig
  N5: Composant2.D4, hc-sr2.Trig
  N6: Composant2.D7, hc-sr2.Echo
  N7: Composant2.B-, M1.pin_2
  N8: Composant2.B+, M1.pin_1
  N9: Composant2.A-, M2.pin_2
  N10: Composant2.A+, M2.pin_1
